# Fritzing sketch fritzing (saved by Fritzing 0.9.4)

parts:
  U1 = NodeMCU V1.0
  DHT1 = DHT22 Humidity and Temperature Sensor
  DHT2 = DHT22 Humidity and Temperature Sensor
  R1 = Resistor [tolerance=±5% resistance=4.7k package=THT]
  R2 = Resistor [tolerance=±5% resistance=4.7k package=THT]
  KY-1 = Keyes Relay [package=THT]

nets:
  N1: U1.D1, DHT2.DATA, R1.Pin_1
  N2: U1.D2, DHT1.DATA, R2.Pin_1
  N3: U1.D3, KY-1.signal
  VDD: U1.3V3, DHT1.VDD, DHT2.VDD, R1.Pin_0, R2.Pin_0, KY-1.power
  GND: U1.GND, DHT1.GND, DHT2.GND, KY-1.ground

custom parts:
  NodeMCU V1.0: ESP8266 based NodeMCU
  Keyes Relay: The Keyes 5V relay module is suitable for SCM development, home appliance control. It uses a 5V~12V TIL control signal which can control DC / AC signal.
